# Fritzing sketch lab4 (saved by Fritzing 0.9.1b)
breadboards: 4

parts:
  LCD1 = LCD screen
  Part1 = Arduino Nano (Rev3.0)
  R1 = Resistor [tolerance=±5% resistance=100 package=THT]
  R2 = Resistor [tolerance=±5% resistance=100 package=THT]
  R3 = Resistor [tolerance=±5% resistance=100 package=THT]
  R4 = Resistor [tolerance=±5% resistance=10 package=THT]
  R5 = Resistor [tolerance=±5% resistance=10 package=THT]
  Potentiometer = mystery part, 3 pins [chip_label=POT]
  R6 = PHOTOCELL [package=photocell]
  R7 = Resistor [tolerance=±5% resistance=10k package=THT]
  RHT1 = Humidity and Temperature Sensor RHT03
  S1 = Pushbutton [package="[THT]"]
  J2 = Piezo Speaker

nets:
  VSS: LCD1.VSS, LCD1.R/W, LCD1.LED-, Part1.GND, R1.Pin_0, R2.Pin_0, R3.Pin_0, Potentiometer.pin3, R7.Pin_1, RHT1.GND_2, S1.Pin_1, S1.Pin_2, J2.pin1
  VDD: LCD1.VDD, Part1.5V, R5.Pin_0, Potentiometer.pin1, R6.P$1, RHT1.Vcc
  N1: LCD1.V0, Potentiometer.pin2
  N2: LCD1.RS, Part1.D2
  N3: LCD1.E, Part1.D3
  N4: LCD1.DB4, Part1.D8
  N5: LCD1.DB5, Part1.D9
  N6: LCD1.DB6, Part1.D10
  N7: LCD1.DB7, Part1.D11/MOSI
  N8: LCD1.LED+, R4.Pin_1, R5.Pin_1
  N9: Part1.D4, RHT1.Data-signal
  N10: Part1.D5, S1.Pin_3, S1.Pin_4
  N11: Part1.D6, J2.pin2
  N12: Part1.A1, R6.P$2, R7.Pin_0
  N13: R1.Pin_1, R2.Pin_1, R3.Pin_1, R4.Pin_0

notes:
  Lab 4 Notes:
  The DHT11 does not have a resistor because we're using the internal pullup resistor in the Arduino.
  The item next to this note lablled POT is the potentiometer that controls the LCD contrast.
